// Logisim project Ascii_to_binary.circ as structural Verilog: 1 circuit, main circuit main
module main (
);

  wire clock_1_out, controlled_buffer_1_out, keyboard_1_avail;
  wire [6:0] divider_1_rem, keyboard_1_data;

  Clock clock_1 (.out(clock_1_out));
  assign controlled_buffer_1_out = keyboard_1_avail ? clock_1_out : 1'bz;  // Controlled_Buffer controlled_buffer_1
  Keyboard keyboard_1 (
    .clk(controlled_buffer_1_out), .avail(keyboard_1_avail), .data(keyboard_1_data));  // open: re, clr
  Divider #(.width(7)) divider_1 (
    .a(keyboard_1_data), .b(7'b0000010), .upper({7{1'b0}}), .rem(divider_1_rem));  // open: out
  // Probe on divider_1_rem
endmodule
