// Logisim project Decryption.circ as structural Verilog: 1 circuit, main circuit main
module main (
  input  [6:0] in_1,
  input  [6:0] PRIVATE_KEY,
  output [6:0] out_3
);

  wire [2:0] xor_1_out;
  wire [6:0] xor_1_out_2;

  not not_1 (out_3[0], xor_1_out_2[0]);
  not not_2 (out_3[2], xor_1_out_2[2]);
  not not_3 (out_3[4], xor_1_out_2[4]);
  not not_4 (out_3[6], xor_1_out_2[6]);
  assign {xor_1_out_2[6], xor_1_out[2], xor_1_out_2[4], xor_1_out[1], xor_1_out_2[2], xor_1_out[0], xor_1_out_2[0]} = in_1 ^ PRIVATE_KEY;  // XOR_Gate xor_1, 7 bits wide
  Shifter #(.width(3), .shift("rr")) shifter_1 (.in(xor_1_out), .\dist (2'b01), .out({out_3[5], out_3[3], out_3[1]}));

  // Notes on the sheet:
  //   INPUT ENCRYPTED MESSAGE
  //   COMMENTS
  //   Working: 1) XOR with priavte key    2) Invert the even bits     3) Roatate the odd bits
  //   <---- INTERMEDIATE DECRYPTED MESSAGE
  //   FINAL DECRYPTED MESSAGE OUTPUT
endmodule
