// Logisim project Encryption.circ as structural Verilog: 1 circuit, main circuit main
module main (
  input  [6:0] in_1,
  input  [6:0] in_2,
  input  [6:0] in_3,
  output [6:0] out_4
);

  not not_1 (in_2[0], in_1[0]);
  not not_2 (in_2[2], in_1[2]);
  not not_3 (in_2[4], in_1[4]);
  not not_4 (in_2[6], in_1[6]);
  assign out_4 = in_3 ^ in_2;  // XOR_Gate xor_1, 7 bits wide
  Shifter #(.width(3), .shift("rl")) shifter_1 (
    .in({in_1[5], in_1[3], in_1[1]}), .\dist (2'b01), .out({in_2[5], in_2[3], in_2[1]}));

  // Notes on the sheet:
  //   INPUT 7 BIT ASCII
  //   PRIVATE KEY INPUT
  //   BIT SHIFTER
  //   COMMENTS
  //   Working: 1) Even bits are inverted    2)Odd bits are combined and shifted left     3) The intermediate message is the XORed with private key
  //   INTERMEDIATE ENCRYTED MESSAGE
  //   FINAL ENCRYPTED MESSAGE OUTPUT
endmodule
