// Logisim project Decryption.circ as structural Verilog
module Logical_Right_Bit_Shifter (
  input  [2:0] in_1,
  output [2:0] out_2
);


  assign out_2 = {in_1[1:0], in_1[2]};
endmodule

module Decrypter (
  input  [6:0] Input_Encrypted_Message,
  input  [6:0] Private_Key,
  input  No_Input,
  output [6:0] Outuput
);

  wire [2:0] logical_right_bit_shifter_1_out_2, xor_1_out;
  wire [6:0] not_1_out, xor_1_out_2;
  wire [6:6] not_5_out;

  not not_1 (not_1_out[0], xor_1_out_2[0]);
  not not_2 (not_1_out[2], xor_1_out_2[2]);
  not not_3 (not_1_out[4], xor_1_out_2[4]);
  not not_4 (not_1_out[6], xor_1_out_2[6]);
  not not_5 (not_5_out[6], No_Input);
  assign {xor_1_out_2[6], xor_1_out[2], xor_1_out_2[4], xor_1_out[1], xor_1_out_2[2], xor_1_out[0], xor_1_out_2[0]} = Input_Encrypted_Message ^ Private_Key;  // XOR_Gate xor_1, 7 bits wide
  Logical_Right_Bit_Shifter logical_right_bit_shifter_1 (.in_1(xor_1_out), .out_2(logical_right_bit_shifter_1_out_2));
  assign Outuput = {not_1_out[6], logical_right_bit_shifter_1_out_2[2], not_1_out[4], logical_right_bit_shifter_1_out_2[1], not_1_out[2], logical_right_bit_shifter_1_out_2[0], not_1_out[0]} & {7{not_5_out[6]}};  // AND_Gate and_1, 7 bits wide

  // Notes on the sheet:
  //   COMMENTS
  //   Working: 1) XOR with priavte key    2) Invert the even bits     3) Roatate the odd bits
  //   <---- INTERMEDIATE DECRYPTED MESSAGE
endmodule
