// Logisim project EMDS.circ as structural Verilog: 8 circuits, main circuit main
module main (
  output [3:0] out_1,
  output [3:0] Enter_Password,
  output [6:0] Key,
  output [6:0] Key_2
);

  wire _0_2_out, _0_out, _1_2_out, _1_out, clock_1_out, clock_2_out, keyboard_1_avail, keyboard_2_avail,
       messenger_1_communication_enabled, messenger_1_display_clock, messenger_1_incoming_monitor_clock,
       messenger_2_communication_enabled, messenger_2_display_clock, messenger_2_incoming_monitor_clock,
       X_2_out, X_out;
  wire [1:0] messenger_1_outgoing_data, messenger_2_outgoing_data;
  wire [6:0] keyboard_1_data, keyboard_2_data, messenger_1_encrypted_text, messenger_1_incoming_monitor,
       messenger_1_outgoing_monitor, messenger_2_encrypted_text, messenger_2_incoming_monitor,
       messenger_2_outgoing_monitor;

  TTY tty_1 (.data(messenger_1_incoming_monitor), .clk(messenger_1_incoming_monitor_clock));  // open: we, clr
  Clock clock_1 (.out(clock_1_out));
  LED Enabled (.in(messenger_1_communication_enabled));
  Button _1 (.out(_1_out));
  Button _0 (.out(_0_out));
  Button X (.out(X_out));
  TTY tty_2 (.data(messenger_1_encrypted_text));  // open: clk, we, clr
  TTY tty_3 (.data(messenger_1_outgoing_monitor), .clk(messenger_1_display_clock));  // open: we, clr
  Messenger messenger_1 (
    .Clock(clock_1_out), .Enable(1'b1), .Incoming_Monitor_Clock(messenger_1_incoming_monitor_clock),
    .Incoming_Monitor(messenger_1_incoming_monitor), .Display_CLock(messenger_1_display_clock),
    .Keyboard_IA(keyboard_1_avail), .Keyboard_Input(keyboard_1_data),
    .Outgoing_Monitor(messenger_1_outgoing_monitor), .Encrypted_Text(messenger_1_encrypted_text),
    ._0_button(_0_out), ._1_button(_1_out), .Reset_button(X_out),
    .Communication_enabled(messenger_1_communication_enabled), .Outgoing_Data(messenger_1_outgoing_data),
    .Incoming_Data(messenger_2_outgoing_data), .Key(Key), .Password(out_1));
  Keyboard keyboard_1 (
    .clk(messenger_1_display_clock), .avail(keyboard_1_avail), .data(keyboard_1_data));  // open: re, clr
  TTY tty_4 (.data(messenger_2_incoming_monitor), .clk(messenger_2_incoming_monitor_clock));  // open: we, clr
  Clock clock_2 (.out(clock_2_out));
  LED Enabled_2 (.in(messenger_2_communication_enabled));
  Button _0_2 (.out(_0_2_out));
  Button _1_2 (.out(_1_2_out));
  TTY tty_5 (.data(messenger_2_encrypted_text));  // open: clk, we, clr
  TTY tty_6 (.data(messenger_2_outgoing_monitor), .clk(messenger_2_display_clock));  // open: we, clr
  Button X_2 (.out(X_2_out));
  Messenger messenger_2 (
    .Clock(clock_2_out), .Enable(1'b1), .Incoming_Monitor_Clock(messenger_2_incoming_monitor_clock),
    .Incoming_Monitor(messenger_2_incoming_monitor), .Display_CLock(messenger_2_display_clock),
    .Keyboard_IA(keyboard_2_avail), .Keyboard_Input(keyboard_2_data),
    .Outgoing_Monitor(messenger_2_outgoing_monitor), .Encrypted_Text(messenger_2_encrypted_text),
    ._0_button(_0_2_out), ._1_button(_1_2_out), .Reset_button(X_2_out),
    .Communication_enabled(messenger_2_communication_enabled), .Outgoing_Data(messenger_2_outgoing_data),
    .Incoming_Data(messenger_1_outgoing_data), .Key(Key_2), .Password(Enter_Password));
  Keyboard keyboard_2 (
    .clk(messenger_2_display_clock), .avail(keyboard_2_avail), .data(keyboard_2_data));  // open: re, clr

  // Notes on the sheet:
  //   INCOMING TEXT
  //   Enter Password
  //   ENCRYPTED MESSAGE OF B
  //   OUTGOING TEXT
  //   Enter Message Here
  //   INCOMING TEXT
  //   ENCRYPTED MESSAGE OF A
  //   OUTGOING TEXT
  //   Enter Message Here
endmodule

module Messenger (
  input  Keyboard_IA,
  input  [6:0] Keyboard_Input,
  input  Clock,
  input  Reset_button,
  input  _0_button,
  input  _1_button,
  input  Enable,
  input  [1:0] Incoming_Data,
  output Incoming_Monitor_Clock,
  output [6:0] Incoming_Monitor,
  output Display_CLock,
  output [6:0] Outgoing_Monitor,
  output [6:0] Key,
  output [3:0] Password,
  output [1:0] Outgoing_Data,
  output Communication_enabled,
  output [6:0] Encrypted_Text
);

  wire and_1_out, Encoder_clock_output, Encoder_op_when, Encoder_output, Receiver_incoming_clock,
       Receiver_incoming_message;
  wire [6:0] Encrypter_encrypted_message;

  Password_Checker password_checker_1 (
    .Password(Password), .Switch_Off(Reset_button), .Clock(Clock), ._0_Button(_0_button),
    ._1_Button(_1_button), .Verified_Output(Communication_enabled));
  and and_1 (and_1_out, Communication_enabled, Clock);
  Decrypter Decrypter (.Input_Encrypted_Message(Encrypted_Text), .Private_Key(7'b1000011), .Outuput(Incoming_Monitor));
  assign Display_CLock = Keyboard_IA ? Encoder_clock_output : 1'bz;  // Controlled_Buffer controlled_buffer_1
  Encrypter Encrypter (
    .Input_7bit_Ascii(Keyboard_Input), .Private_Key_Input(7'b1000011),
    .Encrypted_Message(Encrypter_encrypted_message));
  Encoder Encoder (
    .Clock(and_1_out), .Enable(Enable), .Output(Encoder_output), .Input_Available(Keyboard_IA),
    .Clock_Output(Encoder_clock_output), .op_when(Encoder_op_when), .ASCII_Data(Encrypter_encrypted_message));
  Decoder Decoder (
    .CLOCK(and_1_out), .SerialIn(Receiver_incoming_message), .Enable(Enable),
    .OP_CLOCK(Receiver_incoming_clock), .ASCII(Encrypted_Text), .OP_CLOCK_2(Incoming_Monitor_Clock));
  Transmitter Transmitter (
    .Outgoing_message(Encoder_output), .Outgoing_clock(Encoder_op_when), .Outgoing_data(Outgoing_Data));
  Receiver Receiver (
    .Incoming_Data(Incoming_Data), .Incoming_Message(Receiver_incoming_message),
    .Incoming_Clock(Receiver_incoming_clock));

  assign Key = 7'b1000011;
  assign Outgoing_Monitor = Keyboard_Input;
endmodule

module Verfier (
  input  [3:0] _4_Bit_Password,
  input  Switch_Off,
  output Verifier_Output
);

  wire and_1_out, and_2_out, and_3_out, and_4_out, and_5_out, and_6_out, and_7_out, and_8_out, and_9_out,
       nor_1_out, nor_2_out, nor_3_out, nor_4_out, not_1_out, not_2_out, not_3_out, not_4_out, not_5_out,
       not_6_out, not_7_out, not_8_out, not_9_out;

  not not_1 (not_1_out, Switch_Off);
  not not_2 (not_2_out, _4_Bit_Password[3]);
  not not_3 (not_3_out, 1'b0);
  not not_4 (not_4_out, _4_Bit_Password[2]);
  not not_5 (not_5_out, 1'b1);
  not not_6 (not_6_out, _4_Bit_Password[1]);
  not not_7 (not_7_out, 1'b0);
  not not_8 (not_8_out, _4_Bit_Password[0]);
  not not_9 (not_9_out, 1'b1);
  and and_1 (and_1_out, not_2_out, 1'b0);
  and and_2 (and_2_out, _4_Bit_Password[3], not_3_out);
  and and_3 (and_3_out, not_4_out, 1'b1);
  and and_4 (and_4_out, _4_Bit_Password[2], not_5_out);
  and and_5 (and_5_out, not_6_out, 1'b0);
  and and_6 (and_6_out, _4_Bit_Password[1], not_7_out);
  and and_7 (and_7_out, not_8_out, 1'b1);
  and and_8 (and_8_out, _4_Bit_Password[0], not_9_out);
  nor nor_1 (nor_1_out, and_1_out, and_2_out);
  nor nor_2 (nor_2_out, and_3_out, and_4_out);
  nor nor_3 (nor_3_out, and_5_out, and_6_out);
  nor nor_4 (nor_4_out, and_7_out, and_8_out);
  and and_9 (and_9_out, nor_1_out, nor_2_out, nor_3_out, nor_4_out);
  and and_10 (Verifier_Output, and_9_out, not_1_out);

  // Notes on the sheet:
  //   A3
  //   B3
  //   A2
  //   B2
  //   A1
  //   B1
  //   A0
  //   B0
  //   A=B
endmodule

module DeMux (
  input  Switch_Off,
  input  Clock,
  input  Input_Button_Trigger,
  input  S1,
  input  S0,
  output Op_0,
  output Op_1,
  output Op_2,
  output Op_3
);

  wire and_1_out, and_2_out, and_3_out, and_4_out, and_5_out, and_6_out, and_7_out, and_8_out, not_1_out,
       not_2_out;

  not not_1 (not_1_out, S1);
  not not_2 (not_2_out, S0);
  and and_1 (and_1_out, Input_Button_Trigger, not_1_out, not_2_out);
  and and_2 (and_2_out, Input_Button_Trigger, not_1_out, S0);
  and and_3 (and_3_out, Input_Button_Trigger, S1, not_2_out);
  and and_4 (and_4_out, Input_Button_Trigger, S1, S0);
  and and_5 (and_5_out, not_1_out, not_2_out);
  and and_6 (and_6_out, not_1_out, S0);
  and and_7 (and_7_out, not_2_out, S1);
  and and_8 (and_8_out, S0, S1);
  D_Flip_Flop d_ff_1 (.clk(Clock), .D(and_1_out), .Q(Op_0), .en(and_5_out), .reset(Switch_Off));  // open: Qn, preset
  D_Flip_Flop d_ff_2 (.clk(Clock), .D(and_2_out), .Q(Op_1), .en(and_6_out), .reset(Switch_Off));  // open: Qn, preset
  D_Flip_Flop d_ff_3 (.clk(Clock), .D(and_3_out), .Q(Op_2), .en(and_7_out), .reset(Switch_Off));  // open: Qn, preset
  D_Flip_Flop d_ff_4 (.clk(Clock), .D(and_4_out), .Q(Op_3), .en(and_8_out), .reset(Switch_Off));  // open: Qn, preset
endmodule

module _3_Bit_Counter (
  input  Clock,
  input  Switch_Off,
  output Bit___1,
  output Bit___2
);

  J_K_Flip_Flop #(.trigger("falling")) j_k_ff_1 (
    .J(1'b1), .clk(Clock), .K(1'b1), .Q(Bit___1), .reset(Switch_Off));  // open: Qn, preset, en
  J_K_Flip_Flop #(.trigger("falling")) j_k_ff_2 (
    .J(Bit___1), .clk(Clock), .K(Bit___1), .Q(Bit___2), .reset(Switch_Off));  // open: Qn, preset, en
endmodule

module Password_Checker (
  input  Clock,
  input  Switch_Off,
  input  _0_Button,
  input  _1_Button,
  output [3:0] Password,
  output Verified_Output
);

  wire _3_Bit_Counter_bit___1, _3_Bit_Counter_bit___2, and_1_out, not_1_out, or_1_out;

  and and_1 (and_1_out, not_1_out, _1_Button);
  not not_1 (not_1_out, _0_Button);
  or or_1 (or_1_out, _1_Button, _0_Button);
  _3_Bit_Counter _3_Bit_Counter (
    .Clock(or_1_out), .Switch_Off(Switch_Off), .Bit___1(_3_Bit_Counter_bit___1),
    .Bit___2(_3_Bit_Counter_bit___2));
  DeMux De_Mux (
    .Clock(Clock), .Input_Button_Trigger(and_1_out), .Switch_Off(Switch_Off), .S1(_3_Bit_Counter_bit___2),
    .S0(_3_Bit_Counter_bit___1), .Op_0(Password[1]), .Op_1(Password[2]), .Op_2(Password[3]),
    .Op_3(Password[0]));
  Verfier Verifier (._4_Bit_Password(Password), .Switch_Off(Switch_Off), .Verifier_Output(Verified_Output));
endmodule

module Transmitter (
  input  Outgoing_message,
  input  Outgoing_clock,
  output [1:0] Outgoing_data
);


  assign Outgoing_data = {Outgoing_clock, Outgoing_message};
endmodule

module Receiver (
  input  [1:0] Incoming_Data,
  output Incoming_Message,
  output Incoming_Clock
);


  assign Incoming_Clock = Incoming_Data[1];
  assign Incoming_Message = Incoming_Data[0];
endmodule
