// Logisim project Encryption.circ as structural Verilog: 4 circuits, main circuit main
module main (
  input  [6:0] Input,
  input  [6:0] Key,
  output [6:0] out_3
);

  wire [6:0] encrypter_1_encrypted_message, n0_checker_1_out_2;

  _0_Checker u_0_checker_1 (.in_1(Input), .out_2(n0_checker_1_out_2));
  Encrypter encrypter_1 (
    .Input_7bit_Ascii(Input), .Private_Key_Input(Key), .Encrypted_Message(encrypter_1_encrypted_message));
  assign out_3 = encrypter_1_encrypted_message & n0_checker_1_out_2;  // AND_Gate and_1, 7 bits wide
endmodule

module Logical_Left_Bit_shifter (
  input  [2:0] in_1,
  output [2:0] out_2
);


  assign out_2 = {in_1[0], in_1[2:1]};
endmodule

module Encrypter (
  input  [6:0] Input_7bit_Ascii,
  input  [6:0] Private_Key_Input,
  output [6:0] Encrypted_Message
);

  wire [2:0] logical_left_bit_shifter_1_out_2;
  wire [6:0] not_1_out;

  not not_1 (not_1_out[0], Input_7bit_Ascii[0]);
  not not_2 (not_1_out[2], Input_7bit_Ascii[2]);
  not not_3 (not_1_out[4], Input_7bit_Ascii[4]);
  not not_4 (not_1_out[6], Input_7bit_Ascii[6]);
  assign Encrypted_Message = Private_Key_Input ^ {not_1_out[6], logical_left_bit_shifter_1_out_2[2], not_1_out[4], logical_left_bit_shifter_1_out_2[1], not_1_out[2], logical_left_bit_shifter_1_out_2[0], not_1_out[0]};  // XOR_Gate xor_1, 7 bits wide
  Logical_Left_Bit_shifter logical_left_bit_shifter_1 (
    .in_1({Input_7bit_Ascii[5], Input_7bit_Ascii[3], Input_7bit_Ascii[1]}),
    .out_2(logical_left_bit_shifter_1_out_2));

  // Notes on the sheet:
  //   COMMENTS
  //   BIT SHIFTER
  //   Working: 1) Even bits are inverted    2)Odd bits are combined and shifted left     3) The intermediate message is the XORed with private key
  //   <-
  //   |
  //   INTERMEDIATE ENCRYTED MESSAGE
endmodule

module _0_Checker (
  input  [6:0] in_1,
  output [6:0] out_2
);

  wire and_1_out, and_2_out, and_3_out, and_4_out, and_5_out, and_6_out, and_7_out, and_8_out, and_9_out,
       and_10_out, and_11_out, and_12_out, and_13_out, and_14_out, and_15_out, nor_1_out, nor_2_out,
       nor_3_out, nor_4_out, nor_5_out, nor_6_out, nor_7_out, not_1_out, not_2_out, not_3_out, not_4_out,
       not_5_out, not_6_out, not_7_out, not_8_out, not_9_out, not_10_out, not_11_out, not_12_out, not_13_out,
       not_14_out;

  not not_1 (not_1_out, in_1[0]);
  not not_2 (not_2_out, 1'b0);
  not not_3 (not_3_out, in_1[1]);
  not not_4 (not_4_out, 1'b0);
  not not_5 (not_5_out, in_1[2]);
  not not_6 (not_6_out, 1'b0);
  not not_7 (not_7_out, in_1[3]);
  not not_8 (not_8_out, 1'b0);
  not not_9 (not_9_out, in_1[4]);
  not not_10 (not_10_out, 1'b0);
  not not_11 (not_11_out, in_1[5]);
  not not_12 (not_12_out, 1'b0);
  not not_13 (not_13_out, in_1[6]);
  not not_14 (not_14_out, 1'b0);
  and and_1 (and_1_out, not_1_out, 1'b0);
  and and_2 (and_2_out, in_1[0], not_2_out);
  and and_3 (and_3_out, not_3_out, 1'b0);
  and and_4 (and_4_out, in_1[1], not_4_out);
  and and_5 (and_5_out, not_5_out, 1'b0);
  and and_6 (and_6_out, in_1[2], not_6_out);
  and and_7 (and_7_out, not_7_out, 1'b0);
  and and_8 (and_8_out, in_1[3], not_8_out);
  and and_9 (and_9_out, not_9_out, 1'b0);
  and and_10 (and_10_out, in_1[4], not_10_out);
  and and_11 (and_11_out, not_11_out, 1'b0);
  and and_12 (and_12_out, in_1[5], not_12_out);
  and and_13 (and_13_out, not_13_out, 1'b0);
  and and_14 (and_14_out, in_1[6], not_14_out);
  nor nor_1 (nor_1_out, and_1_out, and_2_out);
  nor nor_2 (nor_2_out, and_3_out, and_4_out);
  nor nor_3 (nor_3_out, and_5_out, and_6_out);
  nor nor_4 (nor_4_out, and_7_out, and_8_out);
  nor nor_5 (nor_5_out, and_9_out, and_10_out);
  nor nor_6 (nor_6_out, and_11_out, and_12_out);
  nor nor_7 (nor_7_out, and_13_out, and_14_out);
  not not_15 (out_2[6], and_15_out);
  and and_15 (and_15_out, nor_1_out, nor_2_out, nor_3_out, nor_4_out, nor_5_out, nor_6_out, nor_7_out);

  assign out_2[5:0] = {6{out_2[6]}};

  // Notes on the sheet:
  //   A6
  //   B6
  //   A5
  //   B5
  //   A4
  //   B4
  //   A3
  //   B3
  //   A2
  //   B2
  //   A1
  //   B1
  //   A0
  //   B0
endmodule
