// Logisim project InputOutput.circ as structural Verilog: 3 circuits, main circuit main
module main (
);

  wire _0_2_out, _0_3_out, _0_4_out, _0_5_out, _0_6_out, _0_7_out, _0_8_out, _0_out, _1_2_out, _1_3_out,
       _1_4_out, _1_5_out, _1_6_out, _1_7_out, _1_8_out, _1_out, and_1_out, and_2_out, and_3_out, and_4_out,
       and_5_out, and_6_out, and_7_out, and_8_out, and_9_out, and_10_out, and_11_out, and_12_out,
       button_1_out, button_2_out, clock_1_out, clock_2_out, clock_3_out, clock_4_out,
       controlled_buffer_1_out, controlled_buffer_2_out, keyboard_1_avail, keyboard_2_avail, not_1_out,
       not_2_out, not_3_out, not_4_out, not_5_out, not_6_out, not_7_out, not_8_out, or_1_out, or_2_out,
       or_3_out, or_4_out, or_5_out, or_6_out, or_7_out, or_8_out, verifier_1_a_b, verifier_2_a_b;
  wire [3:0] d_ff_4_q, d_ff_8_q;
  wire [6:0] Delivery_System_output_a, Delivery_System_output_b, keyboard_1_data, keyboard_2_data;

  and and_1 (and_1_out, clock_1_out, verifier_1_a_b);
  Clock clock_1 (.out(clock_1_out));
  Clock clock_2 (.out(clock_2_out));
  Button button_1 (.out(button_1_out));
  TTY tty_1 (.data(keyboard_1_data), .clk(and_1_out));  // open: we, clr
  assign controlled_buffer_1_out = keyboard_1_avail ? and_1_out : 1'bz;  // Controlled_Buffer controlled_buffer_1
  and and_2 (and_2_out, not_1_out, _1_out);
  not not_1 (not_1_out, _0_out);
  Button _0 (.out(_0_out));
  Keyboard keyboard_1 (
    .clk(controlled_buffer_1_out), .avail(keyboard_1_avail), .data(keyboard_1_data));  // open: re, clr
  or or_1 (or_1_out, _1_out, _0_out);
  Button _1 (.out(_1_out));
  LED led_1 (.in(verifier_1_a_b));
  D_Flip_Flop d_ff_1 (
    .clk(clock_2_out), .D(and_2_out), .Q(d_ff_4_q[3]), .en(or_1_out), .reset(button_1_out));  // open: Qn, preset
  and and_3 (and_3_out, not_2_out, _1_2_out);
  not not_2 (not_2_out, _0_2_out);
  Button _0_2 (.out(_0_2_out));
  Button _1_2 (.out(_1_2_out));
  TTY tty_2 (.data(Delivery_System_output_a), .clk(and_4_out));  // open: we, clr
  and and_4 (and_4_out, and_7_out, and_1_out);
  D_Flip_Flop d_ff_2 (
    .clk(clock_2_out), .D(and_3_out), .Q(d_ff_4_q[2]), .en(or_2_out), .reset(button_1_out));  // open: Qn, preset
  or or_2 (or_2_out, _1_2_out, _0_2_out);
  Verifier verifier_1 (.in_1(d_ff_4_q), .A_B(verifier_1_a_b));
  and and_5 (and_5_out, not_3_out, _1_3_out);
  not not_3 (not_3_out, _0_3_out);
  Button _0_3 (.out(_0_3_out));
  Button _1_3 (.out(_1_3_out));
  D_Flip_Flop d_ff_3 (
    .clk(clock_2_out), .D(and_5_out), .Q(d_ff_4_q[1]), .en(or_3_out), .reset(button_1_out));  // open: Qn, preset
  and and_6 (and_6_out, not_4_out, _1_4_out);
  not not_4 (not_4_out, _0_4_out);
  or or_3 (or_3_out, _1_3_out, _0_3_out);
  Button _0_4 (.out(_0_4_out));
  or or_4 (or_4_out, _1_4_out, _0_4_out);
  Button _1_4 (.out(_1_4_out));
  Delivery_System Delivery_System (
    .Input_A(keyboard_1_data), .Output_A(Delivery_System_output_a), .Output_B(Delivery_System_output_b),
    .Input_B(keyboard_2_data));
  D_Flip_Flop d_ff_4 (
    .clk(clock_2_out), .D(and_6_out), .Q(d_ff_4_q[0]), .en(or_4_out), .reset(button_1_out));  // open: Qn, preset
  Clock clock_3 (.out(clock_3_out));
  Clock clock_4 (.out(clock_4_out));
  Button button_2 (.out(button_2_out));
  and and_7 (and_7_out, clock_3_out, verifier_2_a_b);
  not not_5 (not_5_out, _0_5_out);
  Button _0_5 (.out(_0_5_out));
  TTY tty_3 (.data(keyboard_2_data), .clk(and_7_out));  // open: we, clr
  assign controlled_buffer_2_out = keyboard_2_avail ? and_7_out : 1'bz;  // Controlled_Buffer controlled_buffer_2
  and and_8 (and_8_out, not_5_out, _1_5_out);
  or or_5 (or_5_out, _1_5_out, _0_5_out);
  Button _1_5 (.out(_1_5_out));
  Keyboard keyboard_2 (
    .clk(controlled_buffer_2_out), .avail(keyboard_2_avail), .data(keyboard_2_data));  // open: re, clr
  D_Flip_Flop d_ff_5 (
    .clk(clock_4_out), .D(and_8_out), .Q(d_ff_8_q[3]), .en(or_5_out), .reset(button_2_out));  // open: Qn, preset
  and and_9 (and_9_out, not_6_out, _1_6_out);
  not not_6 (not_6_out, _0_6_out);
  Button _0_6 (.out(_0_6_out));
  Button _1_6 (.out(_1_6_out));
  and and_10 (and_10_out, and_7_out, and_1_out);
  D_Flip_Flop d_ff_6 (
    .clk(clock_4_out), .D(and_9_out), .Q(d_ff_8_q[2]), .en(or_6_out), .reset(button_2_out));  // open: Qn, preset
  or or_6 (or_6_out, _1_6_out, _0_6_out);
  LED led_2 (.in(verifier_2_a_b));
  TTY tty_4 (.data(Delivery_System_output_b), .clk(and_10_out));  // open: we, clr
  Verifier verifier_2 (.in_1(d_ff_8_q), .A_B(verifier_2_a_b));
  and and_11 (and_11_out, not_7_out, _1_7_out);
  not not_7 (not_7_out, _0_7_out);
  Button _0_7 (.out(_0_7_out));
  Button _1_7 (.out(_1_7_out));
  D_Flip_Flop d_ff_7 (
    .clk(clock_4_out), .D(and_11_out), .Q(d_ff_8_q[1]), .en(or_7_out), .reset(button_2_out));  // open: Qn, preset
  and and_12 (and_12_out, not_8_out, _1_8_out);
  not not_8 (not_8_out, _0_8_out);
  or or_7 (or_7_out, _1_7_out, _0_7_out);
  Button _0_8 (.out(_0_8_out));
  or or_8 (or_8_out, _1_8_out, _0_8_out);
  Button _1_8 (.out(_1_8_out));
  D_Flip_Flop d_ff_8 (
    .clk(clock_4_out), .D(and_12_out), .Q(d_ff_8_q[0]), .en(or_8_out), .reset(button_2_out));  // open: Qn, preset

  // Notes on the sheet:
  //   Switch Off
  //   OUTGOING MESSAGE MONITOR A
  //   KEYBOARD A
  //   INCOMING MESSAGE MONITOR A
  //   PASSWORD IS 0101
  //   Switch Off
  //   OUTGOING MESSAGE MONITOR B
  //   KEYBOARD B
  //   INCOMING MESSAGE MONITOR B
endmodule

module Delivery_System (
  input  [6:0] Input_A,
  input  [6:0] Input_B,
  output [6:0] Output_B,
  output [6:0] Output_A
);


  assign Output_A = Input_B;
  assign Output_B = Input_A;
endmodule

module Verifier (
  input  [3:0] in_1,
  output A_B
);

  wire and_1_out, and_2_out, and_3_out, and_4_out, and_5_out, and_6_out, and_7_out, and_8_out, nor_1_out,
       nor_2_out, nor_3_out, nor_4_out, not_1_out, not_2_out, not_3_out, not_4_out, not_5_out, not_6_out,
       not_7_out, not_8_out;

  not not_1 (not_1_out, in_1[3]);
  not not_2 (not_2_out, 1'b0);
  not not_3 (not_3_out, in_1[2]);
  not not_4 (not_4_out, 1'b1);
  not not_5 (not_5_out, in_1[1]);
  not not_6 (not_6_out, 1'b0);
  not not_7 (not_7_out, in_1[0]);
  not not_8 (not_8_out, 1'b1);
  and and_1 (and_1_out, not_1_out, 1'b0);
  and and_2 (and_2_out, in_1[3], not_2_out);
  and and_3 (and_3_out, not_3_out, 1'b1);
  and and_4 (and_4_out, in_1[2], not_4_out);
  and and_5 (and_5_out, not_5_out, 1'b0);
  and and_6 (and_6_out, in_1[1], not_6_out);
  and and_7 (and_7_out, not_7_out, 1'b1);
  and and_8 (and_8_out, in_1[0], not_8_out);
  nor nor_1 (nor_1_out, and_1_out, and_2_out);
  nor nor_2 (nor_2_out, and_3_out, and_4_out);
  nor nor_3 (nor_3_out, and_5_out, and_6_out);
  nor nor_4 (nor_4_out, and_7_out, and_8_out);
  and and_9 (A_B, nor_1_out, nor_2_out, nor_3_out, nor_4_out);

  // Notes on the sheet:
  //   A3
  //   B3
  //   A2
  //   B2
  //   A1
  //   B1
  //   A0
  //   B0
endmodule
