// Logisim project Logisim-114-128.circ as structural Verilog: 19 circuits, main circuit main
module main (
  output [3:0] out_1,
  output [3:0] Enter_Password,
  output [6:0] Key,
  output [6:0] Key_2
);

  wire _0_2_out, _0_out, _1_2_out, _1_out, clock_1_out, clock_2_out, keyboard_1_avail, keyboard_2_avail,
       messenger_1_communication_enabled, messenger_1_display_clock, messenger_1_incoming_monitor_clock,
       messenger_2_communication_enabled, messenger_2_display_clock, messenger_2_incoming_monitor_clock,
       X_2_out, X_out;
  wire [1:0] messenger_1_outgoing_data, messenger_2_outgoing_data;
  wire [6:0] keyboard_1_data, keyboard_2_data, messenger_1_encrypted_text, messenger_1_incoming_monitor,
       messenger_1_outgoing_monitor, messenger_2_encrypted_text, messenger_2_incoming_monitor,
       messenger_2_outgoing_monitor;

  Clock clock_1 (.out(clock_1_out));
  TTY tty_1 (.data(messenger_1_incoming_monitor), .clk(messenger_1_incoming_monitor_clock));  // open: we, clr
  LED Enabled (.in(messenger_1_communication_enabled));
  Button _1 (.out(_1_out));
  Button _0 (.out(_0_out));
  Button X (.out(X_out));
  TTY tty_2 (.data(messenger_1_encrypted_text), .clk(clock_1_out));  // open: we, clr
  TTY tty_3 (.data(messenger_1_outgoing_monitor), .clk(messenger_1_display_clock));  // open: we, clr
  Messenger messenger_1 (
    .Clock(clock_1_out), .Enable(1'b1), .Incoming_Monitor_Clock(messenger_1_incoming_monitor_clock),
    .Incoming_Monitor(messenger_1_incoming_monitor), .Display_CLock(messenger_1_display_clock),
    .Keyboard_IA(keyboard_1_avail), .Keyboard_Input(keyboard_1_data),
    .Outgoing_Monitor(messenger_1_outgoing_monitor), .Encrypted_Text(messenger_1_encrypted_text),
    ._0_button(_0_out), ._1_button(_1_out), .Reset_button(X_out),
    .Communication_enabled(messenger_1_communication_enabled), .Key(Key), .Password(out_1),
    .Outgoing_Data(messenger_1_outgoing_data), .Incoming_Data(messenger_2_outgoing_data));
  Keyboard keyboard_1 (
    .clk(messenger_1_display_clock), .avail(keyboard_1_avail), .data(keyboard_1_data));  // open: re, clr
  Clock clock_2 (.out(clock_2_out));
  TTY tty_4 (.data(messenger_2_incoming_monitor), .clk(messenger_2_incoming_monitor_clock));  // open: we, clr
  LED Enabled_2 (.in(messenger_2_communication_enabled));
  Button _0_2 (.out(_0_2_out));
  Button _1_2 (.out(_1_2_out));
  TTY tty_5 (.data(messenger_2_encrypted_text), .clk(clock_2_out));  // open: we, clr
  TTY tty_6 (.data(messenger_2_outgoing_monitor), .clk(messenger_2_display_clock));  // open: we, clr
  Button X_2 (.out(X_2_out));
  Messenger messenger_2 (
    .Clock(clock_2_out), .Enable(1'b1), .Incoming_Monitor_Clock(messenger_2_incoming_monitor_clock),
    .Incoming_Monitor(messenger_2_incoming_monitor), .Display_CLock(messenger_2_display_clock),
    .Keyboard_IA(keyboard_2_avail), .Keyboard_Input(keyboard_2_data),
    .Outgoing_Monitor(messenger_2_outgoing_monitor), .Encrypted_Text(messenger_2_encrypted_text),
    ._0_button(_0_2_out), ._1_button(_1_2_out), .Reset_button(X_2_out),
    .Communication_enabled(messenger_2_communication_enabled), .Key(Key_2), .Password(Enter_Password),
    .Outgoing_Data(messenger_2_outgoing_data), .Incoming_Data(messenger_1_outgoing_data));
  Keyboard keyboard_2 (
    .clk(messenger_2_display_clock), .avail(keyboard_2_avail), .data(keyboard_2_data));  // open: re, clr

  // Notes on the sheet:
  //   INCOMING TEXT
  //   Password needs to be entered for both users forcommunication to work
  //   Enter Password
  //   USER 1
  //   The Buttons work like number pad
  //   ENCRYPTED MESSAGE OF B
  //   OUTGOING TEXT
  //   Enter Message Here
  //   A proof of concept for Encryption.
  //   Shows what happens without a Decrypter
  //   ENCRYPTED MESSAGE DELIVERY SYSTEM
  //   INCOMING TEXT
  //   USER 2
  //   The Buttons work like number pad
  //   ENCRYPTED MESSAGE OF A
  //   OUTGOING TEXT
  //   Enter Message Here
endmodule

// Messenger \n Instructions: \n 1. Set clock in logisim to 32Hz or above \n 2. Start simulation ticks (ctrl+k) \n 3. Enter Password using buttons. \n Default pwd: 0101 \n 4. Enter message using keyboard above.
module Messenger (
  input  Keyboard_IA,
  input  [6:0] Keyboard_Input,
  input  Clock,
  input  Reset_button,
  input  _0_button,
  input  _1_button,
  input  Enable,
  input  [1:0] Incoming_Data,
  output Incoming_Monitor_Clock,
  output [6:0] Incoming_Monitor,
  output Display_CLock,
  output [6:0] Outgoing_Monitor,
  output [6:0] Key,
  output [3:0] Password,
  output [1:0] Outgoing_Data,
  output Communication_enabled,
  output [6:0] Encrypted_Text
);

  wire and_1_out, Encoder_clock_output, Encoder_op_when, Encoder_output, Receiver_incoming_clock,
       Receiver_incoming_message;
  wire [6:0] Encrypter_encrypted_message;

  Password_Checker password_checker_1 (
    .Password(Password), .Switch_Off(Reset_button), .Clock(Clock), ._0_Button(_0_button),
    ._1_Button(_1_button), .Verified_Output(Communication_enabled));
  and and_1 (and_1_out, Communication_enabled, Clock);
  Decrypter Decrypter (.Input_Encrypted_Message(Encrypted_Text), .Private_Key(7'b1000011), .Outuput(Incoming_Monitor));
  assign Display_CLock = Keyboard_IA ? Encoder_clock_output : 1'bz;  // Controlled_Buffer controlled_buffer_1
  Encrypter Encrypter (
    .Input_7bit_Ascii(Keyboard_Input), .Private_Key_Input(7'b1000011),
    .Encrypted_Message(Encrypter_encrypted_message));
  Encoder Encoder (
    .Clock(and_1_out), .Enable(Enable), .Output(Encoder_output), .op_when(Encoder_op_when),
    .Input_Available(Keyboard_IA), .Clock_Output(Encoder_clock_output),
    .ASCII_Data(Encrypter_encrypted_message));
  Decoder decoder_1 (
    .CLOCK(and_1_out), .SerialIn(Receiver_incoming_message), .Enable(Enable),
    .OP_CLOCK(Receiver_incoming_clock), .ASCII(Encrypted_Text), .OP_CLOCK_2(Incoming_Monitor_Clock));
  Transmitter Transmitter (
    .Outgoing_message(Encoder_output), .Outgoing_clock(Encoder_op_when), .Outgoing_data(Outgoing_Data));
  Receiver Receiver (
    .Incoming_Data(Incoming_Data), .Incoming_Message(Receiver_incoming_message),
    .Incoming_Clock(Receiver_incoming_clock));

  assign Key = 7'b1000011;
  assign Outgoing_Monitor = Keyboard_Input;
endmodule

module Verfier (
  input  [3:0] _4_Bit_Password,
  input  Switch_Off,
  output Verifier_Output
);

  wire and_1_out, and_2_out, and_3_out, and_4_out, and_5_out, and_6_out, and_7_out, and_8_out, and_9_out,
       nor_1_out, nor_2_out, nor_3_out, nor_4_out, not_1_out, not_2_out, not_3_out, not_4_out, not_5_out,
       not_6_out, not_7_out, not_8_out, not_9_out;

  not not_1 (not_1_out, Switch_Off);
  not not_2 (not_2_out, _4_Bit_Password[3]);
  not not_3 (not_3_out, 1'b0);
  not not_4 (not_4_out, _4_Bit_Password[2]);
  not not_5 (not_5_out, 1'b1);
  not not_6 (not_6_out, _4_Bit_Password[1]);
  not not_7 (not_7_out, 1'b0);
  not not_8 (not_8_out, _4_Bit_Password[0]);
  not not_9 (not_9_out, 1'b1);
  and and_1 (and_1_out, not_2_out, 1'b0);
  and and_2 (and_2_out, _4_Bit_Password[3], not_3_out);
  and and_3 (and_3_out, not_4_out, 1'b1);
  and and_4 (and_4_out, _4_Bit_Password[2], not_5_out);
  and and_5 (and_5_out, not_6_out, 1'b0);
  and and_6 (and_6_out, _4_Bit_Password[1], not_7_out);
  and and_7 (and_7_out, not_8_out, 1'b1);
  and and_8 (and_8_out, _4_Bit_Password[0], not_9_out);
  nor nor_1 (nor_1_out, and_1_out, and_2_out);
  nor nor_2 (nor_2_out, and_3_out, and_4_out);
  nor nor_3 (nor_3_out, and_5_out, and_6_out);
  nor nor_4 (nor_4_out, and_7_out, and_8_out);
  and and_9 (and_9_out, nor_1_out, nor_2_out, nor_3_out, nor_4_out);
  and and_10 (Verifier_Output, and_9_out, not_1_out);

  // Notes on the sheet:
  //   A3
  //   B3
  //   A2
  //   B2
  //   A1
  //   B1
  //   A0
  //   B0
  //   A=B
endmodule

module DeMux (
  input  Switch_Off,
  input  Clock,
  input  Input_Button_Trigger,
  input  S1,
  input  S0,
  output Op_0,
  output Op_1,
  output Op_2,
  output Op_3
);

  wire and_1_out, and_2_out, and_3_out, and_4_out, and_5_out, and_6_out, and_7_out, and_8_out, not_1_out,
       not_2_out;

  not not_1 (not_1_out, S1);
  not not_2 (not_2_out, S0);
  and and_1 (and_1_out, Input_Button_Trigger, not_1_out, not_2_out);
  and and_2 (and_2_out, Input_Button_Trigger, not_1_out, S0);
  and and_3 (and_3_out, Input_Button_Trigger, S1, not_2_out);
  and and_4 (and_4_out, Input_Button_Trigger, S1, S0);
  and and_5 (and_5_out, not_1_out, not_2_out);
  and and_6 (and_6_out, not_1_out, S0);
  and and_7 (and_7_out, not_2_out, S1);
  and and_8 (and_8_out, S0, S1);
  D_Flip_Flop d_ff_1 (.clk(Clock), .D(and_1_out), .Q(Op_0), .en(and_5_out), .reset(Switch_Off));  // open: Qn, preset
  D_Flip_Flop d_ff_2 (.clk(Clock), .D(and_2_out), .Q(Op_1), .en(and_6_out), .reset(Switch_Off));  // open: Qn, preset
  D_Flip_Flop d_ff_3 (.clk(Clock), .D(and_3_out), .Q(Op_2), .en(and_7_out), .reset(Switch_Off));  // open: Qn, preset
  D_Flip_Flop d_ff_4 (.clk(Clock), .D(and_4_out), .Q(Op_3), .en(and_8_out), .reset(Switch_Off));  // open: Qn, preset
endmodule

module _2_Bit_Counter (
  input  Clock,
  input  Switch_Off,
  output Bit___1,
  output Bit___2
);

  J_K_Flip_Flop #(.trigger("falling")) j_k_ff_1 (
    .J(1'b1), .clk(Clock), .K(1'b1), .Q(Bit___1), .reset(Switch_Off));  // open: Qn, preset, en
  J_K_Flip_Flop #(.trigger("falling")) j_k_ff_2 (
    .J(Bit___1), .clk(Clock), .K(Bit___1), .Q(Bit___2), .reset(Switch_Off));  // open: Qn, preset, en
endmodule

module Password_Checker (
  input  Clock,
  input  Switch_Off,
  input  _0_Button,
  input  _1_Button,
  output [3:0] Password,
  output Verified_Output
);

  wire _3_Bit_Counter_bit___1, _3_Bit_Counter_bit___2, and_1_out, not_1_out, or_1_out;

  and and_1 (and_1_out, not_1_out, _1_Button);
  not not_1 (not_1_out, _0_Button);
  or or_1 (or_1_out, _1_Button, _0_Button);
  _2_Bit_Counter _3_Bit_Counter (
    .Clock(or_1_out), .Switch_Off(Switch_Off), .Bit___1(_3_Bit_Counter_bit___1),
    .Bit___2(_3_Bit_Counter_bit___2));
  DeMux De_Mux (
    .Clock(Clock), .Input_Button_Trigger(and_1_out), .Switch_Off(Switch_Off), .S1(_3_Bit_Counter_bit___2),
    .S0(_3_Bit_Counter_bit___1), .Op_0(Password[1]), .Op_1(Password[2]), .Op_2(Password[3]),
    .Op_3(Password[0]));
  Verfier Verifier (._4_Bit_Password(Password), .Switch_Off(Switch_Off), .Verifier_Output(Verified_Output));
endmodule

module Transmitter (
  input  Outgoing_message,
  input  Outgoing_clock,
  output [1:0] Outgoing_data
);


  assign Outgoing_data = {Outgoing_clock, Outgoing_message};
endmodule

module Receiver (
  input  [1:0] Incoming_Data,
  output Incoming_Message,
  output Incoming_Clock
);


  assign Incoming_Clock = Incoming_Data[1];
  assign Incoming_Message = Incoming_Data[0];
endmodule

module Logical_RIght_Bit_Shifter (
  input  [2:0] in_1,
  output [2:0] out_2
);


  assign out_2 = {in_1[1:0], in_1[2]};
endmodule

module Decrypter (
  input  [6:0] Input_Encrypted_Message,
  input  [6:0] Private_Key,
  output [6:0] Outuput
);

  wire [2:0] xor_1_out;
  wire [6:0] xor_1_out_2;

  not not_1 (Outuput[0], xor_1_out_2[0]);
  not not_2 (Outuput[2], xor_1_out_2[2]);
  not not_3 (Outuput[4], xor_1_out_2[4]);
  not not_4 (Outuput[6], xor_1_out_2[6]);
  assign {xor_1_out_2[6], xor_1_out[2], xor_1_out_2[4], xor_1_out[1], xor_1_out_2[2], xor_1_out[0], xor_1_out_2[0]} = Input_Encrypted_Message ^ Private_Key;  // XOR_Gate xor_1, 7 bits wide
  Logical_RIght_Bit_Shifter logical_right_bit_shifter_1 (
    .in_1(xor_1_out), .out_2({Outuput[5], Outuput[3], Outuput[1]}));

  // Notes on the sheet:
  //   COMMENTS
  //   Working: 1) XOR with priavte key    2) Invert the even bits     3) Roatate the odd bits
  //   <---- INTERMEDIATE DECRYPTED MESSAGE
endmodule

module Logical_Left_Bit_Shifter (
  input  [2:0] in_1,
  output [2:0] out_2
);


  assign out_2 = {in_1[0], in_1[2:1]};
endmodule

module Encrypter (
  input  [6:0] Input_7bit_Ascii,
  input  [6:0] Private_Key_Input,
  output [6:0] Encrypted_Message
);

  wire [2:0] logical_left_bit_shifter_1_out_2;
  wire [6:0] n0_checker_1_output, not_1_out, xor_1_out;

  not not_1 (not_1_out[0], Input_7bit_Ascii[0]);
  not not_2 (not_1_out[2], Input_7bit_Ascii[2]);
  not not_3 (not_1_out[4], Input_7bit_Ascii[4]);
  not not_4 (not_1_out[6], Input_7bit_Ascii[6]);
  assign xor_1_out = Private_Key_Input ^ {not_1_out[6], logical_left_bit_shifter_1_out_2[2], not_1_out[4], logical_left_bit_shifter_1_out_2[1], not_1_out[2], logical_left_bit_shifter_1_out_2[0], not_1_out[0]};  // XOR_Gate xor_1, 7 bits wide
  Logical_Left_Bit_Shifter logical_left_bit_shifter_1 (
    .in_1({Input_7bit_Ascii[5], Input_7bit_Ascii[3], Input_7bit_Ascii[1]}),
    .out_2(logical_left_bit_shifter_1_out_2));
  _0_checker u_0_checker_1 (.Input(Input_7bit_Ascii), .Output(n0_checker_1_output));
  assign Encrypted_Message = n0_checker_1_output & xor_1_out;  // AND_Gate and_1, 7 bits wide

  // Notes on the sheet:
  //   COMMENTS
  //   BIT SHIFTER
  //   Working: 1) Even bits are inverted    2)Odd bits are combined and shifted left     3) The intermediate message is the XORed with private key
  //   <-
  //   |
  //   INTERMEDIATE ENCRYTED MESSAGE
endmodule

module _0_checker (
  input  [6:0] Input,
  output [6:0] Output
);

  wire and_1_out, and_2_out, and_3_out, and_4_out, and_5_out, and_6_out, and_7_out, and_8_out, and_9_out,
       and_10_out, and_11_out, and_12_out, and_13_out, and_14_out, and_15_out, nor_1_out, nor_2_out,
       nor_3_out, nor_4_out, nor_5_out, nor_6_out, nor_7_out, not_1_out, not_2_out, not_3_out, not_4_out,
       not_5_out, not_6_out, not_7_out, not_8_out, not_9_out, not_10_out, not_11_out, not_12_out, not_13_out,
       not_14_out;

  not not_1 (not_1_out, Input[0]);
  not not_2 (not_2_out, 1'b0);
  not not_3 (not_3_out, Input[1]);
  not not_4 (not_4_out, 1'b0);
  not not_5 (not_5_out, Input[2]);
  not not_6 (not_6_out, 1'b0);
  not not_7 (not_7_out, Input[3]);
  not not_8 (not_8_out, 1'b0);
  not not_9 (not_9_out, Input[4]);
  not not_10 (not_10_out, 1'b0);
  not not_11 (not_11_out, Input[5]);
  not not_12 (not_12_out, 1'b0);
  not not_13 (not_13_out, Input[6]);
  not not_14 (not_14_out, 1'b0);
  and and_1 (and_1_out, not_1_out, 1'b0);
  and and_2 (and_2_out, Input[0], not_2_out);
  and and_3 (and_3_out, not_3_out, 1'b0);
  and and_4 (and_4_out, Input[1], not_4_out);
  and and_5 (and_5_out, not_5_out, 1'b0);
  and and_6 (and_6_out, Input[2], not_6_out);
  and and_7 (and_7_out, not_7_out, 1'b0);
  and and_8 (and_8_out, Input[3], not_8_out);
  and and_9 (and_9_out, not_9_out, 1'b0);
  and and_10 (and_10_out, Input[4], not_10_out);
  and and_11 (and_11_out, not_11_out, 1'b0);
  and and_12 (and_12_out, Input[5], not_12_out);
  and and_13 (and_13_out, not_13_out, 1'b0);
  and and_14 (and_14_out, Input[6], not_14_out);
  nor nor_1 (nor_1_out, and_1_out, and_2_out);
  nor nor_2 (nor_2_out, and_3_out, and_4_out);
  nor nor_3 (nor_3_out, and_5_out, and_6_out);
  nor nor_4 (nor_4_out, and_7_out, and_8_out);
  nor nor_5 (nor_5_out, and_9_out, and_10_out);
  nor nor_6 (nor_6_out, and_11_out, and_12_out);
  nor nor_7 (nor_7_out, and_13_out, and_14_out);
  and and_15 (and_15_out, nor_1_out, nor_2_out, nor_3_out, nor_4_out, nor_5_out, nor_6_out, nor_7_out);
  not not_15 (Output[6], and_15_out);

  assign Output[5:0] = {6{Output[6]}};

  // Notes on the sheet:
  //   A6
  //   B6
  //   A5
  //   B5
  //   A4
  //   B4
  //   A3
  //   B3
  //   A2
  //   B2
  //   A1
  //   B1
  //   A0
  //   B0
endmodule

module PISO (
  input  D6,
  input  D5,
  input  D4,
  input  D3,
  input  D2,
  input  D1,
  input  D0,
  input  SerialIN,
  input  Clock,
  input  Shift_Load,
  input  Enable,
  input  Clear,
  output SerialOut
);

  wire n1_bit_register_1_q, n1_bit_register_2_q, n1_bit_register_3_q, n1_bit_register_4_q,
       n1_bit_register_5_q, n1_bit_register_6_q;

  _1_Bit_Register u_1_bit_register_1 (
    .CLock(Clock), .SerialIn(SerialIN), .SHIFT_LOAD(Shift_Load), .Din(D6), .Enable(Enable), .Clear(Clear),
    .Q(n1_bit_register_1_q));
  _1_Bit_Register u_1_bit_register_2 (
    .CLock(Clock), .SerialIn(n1_bit_register_1_q), .SHIFT_LOAD(Shift_Load), .Din(D5), .Enable(Enable),
    .Clear(Clear), .Q(n1_bit_register_2_q));
  _1_Bit_Register u_1_bit_register_3 (
    .CLock(Clock), .SerialIn(n1_bit_register_2_q), .SHIFT_LOAD(Shift_Load), .Din(D4), .Enable(Enable),
    .Clear(Clear), .Q(n1_bit_register_3_q));
  _1_Bit_Register u_1_bit_register_4 (
    .CLock(Clock), .SerialIn(n1_bit_register_3_q), .SHIFT_LOAD(Shift_Load), .Din(D3), .Enable(Enable),
    .Clear(Clear), .Q(n1_bit_register_4_q));
  _1_Bit_Register u_1_bit_register_5 (
    .CLock(Clock), .SerialIn(n1_bit_register_4_q), .SHIFT_LOAD(Shift_Load), .Din(D2), .Enable(Enable),
    .Clear(Clear), .Q(n1_bit_register_5_q));
  _1_Bit_Register u_1_bit_register_6 (
    .CLock(Clock), .SerialIn(n1_bit_register_5_q), .SHIFT_LOAD(Shift_Load), .Din(D1), .Enable(Enable),
    .Clear(Clear), .Q(n1_bit_register_6_q));
  _1_Bit_Register u_1_bit_register_7 (
    .CLock(Clock), .SerialIn(n1_bit_register_6_q), .SHIFT_LOAD(Shift_Load), .Din(D0), .Enable(Enable),
    .Clear(Clear), .Q(SerialOut));
endmodule

module _1_Bit_Register (
  input  Din,
  input  CLock,
  input  SerialIn,
  input  SHIFT_LOAD,
  input  Enable,
  input  Clear,
  output Q
);

  wire and_1_out, and_2_out, not_1_out, or_1_out;

  not not_1 (not_1_out, SHIFT_LOAD);
  and and_1 (and_1_out, Din, not_1_out);
  and and_2 (and_2_out, SHIFT_LOAD, SerialIn);
  D_Flip_Flop d_ff_1 (.clk(CLock), .D(or_1_out), .Q(Q), .en(Enable), .reset(Clear));  // open: Qn, preset
  or or_1 (or_1_out, and_1_out, and_2_out);
endmodule

module _3_Bit_Counter (
  input  Clock,
  output Q0,
  output Q1,
  output Q2,
  output _7,
  output _0
);

  wire and_1_out;

  J_K_Flip_Flop j_k_ff_1 (.J(1'b1), .clk(Clock), .K(1'b1), .Q(Q0));  // open: Qn, preset, en, reset
  J_K_Flip_Flop j_k_ff_2 (.J(Q0), .clk(Clock), .K(Q0), .Q(Q1));  // open: Qn, preset, en, reset
  and and_1 (and_1_out, Q0, Q1);
  J_K_Flip_Flop j_k_ff_3 (.J(and_1_out), .clk(Clock), .K(and_1_out), .Q(Q2));  // open: Qn, preset, en, reset
  and and_2 (_7, Q2, Q1, Q0);
  nor nor_1 (_0, Q2, Q1, Q0);
endmodule

module SIPO (
  input  Clock,
  input  SerialIn,
  input  Enable,
  input  Clear,
  output D6,
  output D5,
  output D4,
  output D3,
  output D2,
  output D1,
  output D0
);

  D_Flip_Flop d_ff_1 (.clk(Clock), .D(SerialIn), .Q(D6), .en(Enable), .reset(Clear));  // open: Qn, preset
  D_Flip_Flop d_ff_2 (.clk(Clock), .D(D6), .Q(D5), .en(Enable), .reset(Clear));  // open: Qn, preset
  D_Flip_Flop d_ff_3 (.clk(Clock), .D(D5), .Q(D4), .en(Enable), .reset(Clear));  // open: Qn, preset
  D_Flip_Flop d_ff_4 (.clk(Clock), .D(D4), .Q(D3), .en(Enable), .reset(Clear));  // open: Qn, preset
  D_Flip_Flop d_ff_5 (.clk(Clock), .D(D3), .Q(D2), .en(Enable));  // open: Qn, preset, reset
  D_Flip_Flop d_ff_6 (.clk(Clock), .D(D2), .Q(D1), .en(Enable), .reset(Clear));  // open: Qn, preset
  D_Flip_Flop d_ff_7 (.clk(Clock), .D(D1), .Q(D0), .en(Enable), .reset(Clear));  // open: Qn, preset
endmodule

module Encoder (
  input  Input_Available,
  input  [6:0] ASCII_Data,
  input  Clock,
  input  Enable,
  output Clock_Output,
  output Output,
  output op_when
);

  wire and_1_out, n3_bit_counter_1__7, not_1_out, not_2_out;

  _3_Bit_Counter u_3_bit_counter_1 (.Clock(Clock), ._7(n3_bit_counter_1__7));  // open: Q0, Q1, Q2, _0
  nand nand_1 (Clock_Output, Input_Available, n3_bit_counter_1__7);
  or or_1 (op_when, not_1_out, and_1_out);
  not not_1 (not_1_out, Clock_Output);
  not not_2 (not_2_out, Input_Available);
  and and_1 (and_1_out, not_2_out, n3_bit_counter_1__7);
  PISO piso_1 (
    .Clock(Clock), .Shift_Load(Clock_Output), .D6(ASCII_Data[6]), .D5(ASCII_Data[5]), .D4(ASCII_Data[4]),
    .D3(ASCII_Data[3]), .D2(ASCII_Data[2]), .D1(ASCII_Data[1]), .D0(ASCII_Data[0]), .Enable(Enable),
    .Clear(and_1_out), .SerialOut(Output));  // open: SerialIN

  // Notes on the sheet:
  //   SH/LD should be 0 when counter reaches 7 and input is available
  //   Clear should be 1 when input is not available and counter reaches 7
  //   We would need to transmit clock pulses as well
endmodule

module Decoder (
  input  CLOCK,
  input  SerialIn,
  input  Enable,
  input  OP_CLOCK,
  output [6:0] ASCII,
  output OP_CLOCK_2
);

  SIPO sipo_1 (
    .SerialIn(SerialIn), .Enable(Enable), .Clock(CLOCK), .D6(ASCII[6]), .D5(ASCII[5]), .D4(ASCII[4]),
    .D3(ASCII[3]), .D2(ASCII[2]), .D1(ASCII[1]), .D0(ASCII[0]));  // open: Clear

  assign OP_CLOCK_2 = OP_CLOCK;
endmodule
