// Logisim project en-decode.circ as structural Verilog: 7 circuits, main circuit main
module main (
);

  wire clock_1_out, controlled_buffer_1_out, decoder_1_op_clock_2, encoder_1_clock_output, encoder_1_op_when,
       encoder_1_output, keyboard_1_avail;
  wire [6:0] decoder_1_out_5, keyboard_1_data;

  Clock clock_1 (.out(clock_1_out));
  Encoder encoder_1 (
    .Clock(clock_1_out), .Enable(1'b1), .Input_Available(keyboard_1_avail),
    .Clock_Output(encoder_1_clock_output), .op_when(encoder_1_op_when), .ASCII_Data(keyboard_1_data),
    .Output(encoder_1_output));
  assign controlled_buffer_1_out = keyboard_1_avail ? encoder_1_clock_output : 1'bz;  // Controlled_Buffer controlled_buffer_1
  Keyboard keyboard_1 (
    .clk(controlled_buffer_1_out), .avail(keyboard_1_avail), .data(keyboard_1_data));  // open: re, clr
  Decoder decoder_1 (
    .CLOCK(clock_1_out), .SerialIn(encoder_1_output), .Enable(1'b1), .OP_CLOCK(encoder_1_op_when),
    .out_5(decoder_1_out_5), .OP_CLOCK_2(decoder_1_op_clock_2));
  TTY tty_1 (.data(decoder_1_out_5), .clk(decoder_1_op_clock_2));  // open: we, clr
endmodule

module PISO (
  input  D6,
  input  D5,
  input  D4,
  input  D3,
  input  D2,
  input  D1,
  input  D0,
  input  SerialIN,
  input  Clock,
  input  Shift_Load,
  input  Enable,
  input  Clear,
  output SerialOut
);

  wire n1_bit_register_1_q, n1_bit_register_2_q, n1_bit_register_3_q, n1_bit_register_4_q,
       n1_bit_register_5_q, n1_bit_register_6_q;

  _1_bit_Register u_1_bit_register_1 (
    .CLock(Clock), .SerialIn(SerialIN), .SHIFT_LOAD(Shift_Load), .Din(D6), .Enable(Enable), .Clear(Clear),
    .Q(n1_bit_register_1_q));
  _1_bit_Register u_1_bit_register_2 (
    .CLock(Clock), .SerialIn(n1_bit_register_1_q), .SHIFT_LOAD(Shift_Load), .Din(D5), .Enable(Enable),
    .Clear(Clear), .Q(n1_bit_register_2_q));
  _1_bit_Register u_1_bit_register_3 (
    .CLock(Clock), .SerialIn(n1_bit_register_2_q), .SHIFT_LOAD(Shift_Load), .Din(D4), .Enable(Enable),
    .Clear(Clear), .Q(n1_bit_register_3_q));
  _1_bit_Register u_1_bit_register_4 (
    .CLock(Clock), .SerialIn(n1_bit_register_3_q), .SHIFT_LOAD(Shift_Load), .Din(D3), .Enable(Enable),
    .Clear(Clear), .Q(n1_bit_register_4_q));
  _1_bit_Register u_1_bit_register_5 (
    .CLock(Clock), .SerialIn(n1_bit_register_4_q), .SHIFT_LOAD(Shift_Load), .Din(D2), .Enable(Enable),
    .Clear(Clear), .Q(n1_bit_register_5_q));
  _1_bit_Register u_1_bit_register_6 (
    .CLock(Clock), .SerialIn(n1_bit_register_5_q), .SHIFT_LOAD(Shift_Load), .Din(D1), .Enable(Enable),
    .Clear(Clear), .Q(n1_bit_register_6_q));
  _1_bit_Register u_1_bit_register_7 (
    .CLock(Clock), .SerialIn(n1_bit_register_6_q), .SHIFT_LOAD(Shift_Load), .Din(D0), .Enable(Enable),
    .Clear(Clear), .Q(SerialOut));
endmodule

module _1_bit_Register (
  input  Din,
  input  CLock,
  input  SerialIn,
  input  SHIFT_LOAD,
  input  Enable,
  input  Clear,
  output Q
);

  wire and_1_out, and_2_out, not_1_out, or_1_out;

  not not_1 (not_1_out, SHIFT_LOAD);
  and and_1 (and_1_out, Din, not_1_out);
  and and_2 (and_2_out, SHIFT_LOAD, SerialIn);
  D_Flip_Flop d_ff_1 (.clk(CLock), .D(or_1_out), .Q(Q), .en(Enable), .reset(Clear));  // open: Qn, preset
  or or_1 (or_1_out, and_1_out, and_2_out);
endmodule

module Counter (
  input  Clock,
  output Q0,
  output Q1,
  output Q2,
  output _7,
  output _0
);

  wire and_1_out;

  J_K_Flip_Flop j_k_ff_1 (.J(1'b1), .clk(Clock), .K(1'b1), .Q(Q0));  // open: Qn, preset, en, reset
  J_K_Flip_Flop j_k_ff_2 (.J(Q0), .clk(Clock), .K(Q0), .Q(Q1));  // open: Qn, preset, en, reset
  and and_1 (and_1_out, Q0, Q1);
  J_K_Flip_Flop j_k_ff_3 (.J(and_1_out), .clk(Clock), .K(and_1_out), .Q(Q2));  // open: Qn, preset, en, reset
  and and_2 (_7, Q2, Q1, Q0);
  nor nor_1 (_0, Q2, Q1, Q0);
endmodule

module SIPO (
  input  Clock,
  input  SerialIn,
  input  Enable,
  input  Clear,
  output D6,
  output D5,
  output D4,
  output D3,
  output D2,
  output D1,
  output D0
);

  D_Flip_Flop d_ff_1 (.clk(Clock), .D(SerialIn), .Q(D6), .en(Enable), .reset(Clear));  // open: Qn, preset
  D_Flip_Flop d_ff_2 (.clk(Clock), .D(D6), .Q(D5), .en(Enable), .reset(Clear));  // open: Qn, preset
  D_Flip_Flop d_ff_3 (.clk(Clock), .D(D5), .Q(D4), .en(Enable), .reset(Clear));  // open: Qn, preset
  D_Flip_Flop d_ff_4 (.clk(Clock), .D(D4), .Q(D3), .en(Enable), .reset(Clear));  // open: Qn, preset
  D_Flip_Flop d_ff_5 (.clk(Clock), .D(D3), .Q(D2), .en(Enable));  // open: Qn, preset, reset
  D_Flip_Flop d_ff_6 (.clk(Clock), .D(D2), .Q(D1), .en(Enable), .reset(Clear));  // open: Qn, preset
  D_Flip_Flop d_ff_7 (.clk(Clock), .D(D1), .Q(D0), .en(Enable), .reset(Clear));  // open: Qn, preset
endmodule

module Encoder (
  input  Input_Available,
  input  [6:0] ASCII_Data,
  input  Clock,
  input  Enable,
  output Clock_Output,
  output op_when,
  output Output
);

  wire and_1_out, counter_1__7, not_1_out, not_2_out;

  Counter counter_1 (.Clock(Clock), ._7(counter_1__7));  // open: Q0, Q1, Q2, _0
  nand nand_1 (Clock_Output, Input_Available, counter_1__7);
  or or_1 (op_when, not_1_out, and_1_out);
  not not_1 (not_1_out, Clock_Output);
  not not_2 (not_2_out, Input_Available);
  and and_1 (and_1_out, not_2_out, counter_1__7);
  PISO piso_1 (
    .Clock(Clock), .Shift_Load(Clock_Output), .D6(ASCII_Data[6]), .D5(ASCII_Data[5]), .D4(ASCII_Data[4]),
    .D3(ASCII_Data[3]), .D2(ASCII_Data[2]), .D1(ASCII_Data[1]), .D0(ASCII_Data[0]), .Enable(Enable),
    .Clear(and_1_out), .SerialOut(Output));  // open: SerialIN

  // Notes on the sheet:
  //   SH/LD should be 0 when counter reaches 7 and input is available
  //   Clear should be 1 when input is not available and counter reaches 7
  //   We would need to transmit clock pulses as well
endmodule

module Decoder (
  input  CLOCK,
  input  SerialIn,
  input  Enable,
  input  OP_CLOCK,
  output [6:0] out_5,
  output OP_CLOCK_2
);

  SIPO sipo_1 (
    .SerialIn(SerialIn), .Enable(Enable), .Clock(CLOCK), .D6(out_5[6]), .D5(out_5[5]), .D4(out_5[4]),
    .D3(out_5[3]), .D2(out_5[2]), .D1(out_5[1]), .D0(out_5[0]));  // open: Clear

  assign OP_CLOCK_2 = OP_CLOCK;
endmodule
